// Logisim project processor.circ as structural Verilog
module InstructionMemory (
  input  [23:0] Addr,
  output [31:0] Instruction
);

  ROM #(.addrWidth(24), .dataWidth(32)) InstructionMemory (.addr(Addr), .data(Instruction));
endmodule

module RegisterFile (
  input  [31:0] rd_data_in,
  input  [4:0] rs1_addr,
  input  [4:0] rs2_addr,
  input  [4:0] rd_addr,
  input  reg_write_en,
  output [31:0] rs1_data,
  output [31:0] rs2_data
);

  wire clk, w0, w1, w2, w3, w4, w5, w6, w7, w8, w9, w10, w11, w12, w13, w14, w15, w16, w17, w18, w19, w20,
       w21, w22, w23, w24, w25, w26, w27, w28, w29, w30, w31;
  wire [31:0] q0, q1, q2, q3, q4, q5, q6, q7, q8, q9, q10, q11, q12, q13, q14, q15, q16, q17, q18, q19, q20,
       q21, q22, q23, q24, q25, q26, q27, q28, q29, q30, q31;

  Clock u_clk (.out(clk));
  Multiplexer #(.select(5), .width(32)) multiplexer_1 (
    .in0(q0), .in1(q1), .in2(q2), .in3(q3), .in4(q4), .in5(q5), .in6(q6), .in7(q7), .in8(q8), .in9(q9),
    .in10(q10), .in11(q11), .in12(q12), .in13(q13), .in14(q14), .in15(q15), .in16(q16), .in17(q17),
    .in18(q18), .in19(q19), .in20(q20), .in21(q21), .in22(q22), .in23(q23), .in24(q24), .in25(q25),
    .in26(q26), .in27(q27), .in28(q28), .in29(q29), .in30(q30), .in31(q31), .out(rs1_data), .sel(rs1_addr));
  Demultiplexer #(.select(5)) demultiplexer_1 (
    .out0(w0), .out1(w1), .out2(w2), .out3(w3), .out4(w4), .out5(w5), .out6(w6), .out7(w7), .out8(w8),
    .out9(w9), .out10(w10), .out11(w11), .out12(w12), .out13(w13), .out14(w14), .out15(w15), .out16(w16),
    .out17(w17), .out18(w18), .out19(w19), .out20(w20), .out21(w21), .out22(w22), .out23(w23), .out24(w24),
    .out25(w25), .out26(w26), .out27(w27), .out28(w28), .out29(w29), .out30(w30), .out31(w31),
    .in(reg_write_en), .sel(rd_addr));
  Multiplexer #(.select(5), .width(32)) multiplexer_2 (
    .in0(q0), .in1(q1), .in2(q2), .in3(q3), .in4(q4), .in5(q5), .in6(q6), .in7(q7), .in8(q8), .in9(q9),
    .in10(q10), .in11(q11), .in12(q12), .in13(q13), .in14(q14), .in15(q15), .in16(q16), .in17(q17),
    .in18(q18), .in19(q19), .in20(q20), .in21(q21), .in22(q22), .in23(q23), .in24(q24), .in25(q25),
    .in26(q26), .in27(q27), .in28(q28), .in29(q29), .in30(q30), .in31(q31), .out(rs2_data), .sel(rs2_addr));
  Register #(.width(32)) register_1 (.D({32{1'b0}}), .en(w0), .clk(clk), .Q(q0));  // open: clr
  Register #(.width(32)) register_2 (.D(rd_data_in), .en(w4), .clk(clk), .Q(q4));  // open: clr
  Register #(.width(32)) register_3 (.D(rd_data_in), .en(w8), .clk(clk), .Q(q8));  // open: clr
  Register #(.width(32)) register_4 (.D(rd_data_in), .en(w12), .clk(clk), .Q(q12));  // open: clr
  Register #(.width(32)) register_5 (.D(rd_data_in), .en(w16), .clk(clk), .Q(q16));  // open: clr
  Register #(.width(32)) register_6 (.D(rd_data_in), .en(w20), .clk(clk), .Q(q20));  // open: clr
  Register #(.width(32)) register_7 (.D(rd_data_in), .en(w24), .clk(clk), .Q(q24));  // open: clr
  Register #(.width(32)) register_8 (.D(rd_data_in), .en(w28), .clk(clk), .Q(q28));  // open: clr
  Register #(.width(32)) register_9 (.D(rd_data_in), .en(w1), .clk(clk), .Q(q1));  // open: clr
  Register #(.width(32)) register_10 (.D(rd_data_in), .en(w5), .clk(clk), .Q(q5));  // open: clr
  Register #(.width(32)) register_11 (.D(rd_data_in), .en(w9), .clk(clk), .Q(q9));  // open: clr
  Register #(.width(32)) register_12 (.D(rd_data_in), .en(w13), .clk(clk), .Q(q13));  // open: clr
  Register #(.width(32)) register_13 (.D(rd_data_in), .en(w17), .clk(clk), .Q(q17));  // open: clr
  Register #(.width(32)) register_14 (.D(rd_data_in), .en(w21), .clk(clk), .Q(q21));  // open: clr
  Register #(.width(32)) register_15 (.D(rd_data_in), .en(w25), .clk(clk), .Q(q25));  // open: clr
  Register #(.width(32)) register_16 (.D(rd_data_in), .en(w29), .clk(clk), .Q(q29));  // open: clr
  Register #(.width(32)) register_17 (.D(rd_data_in), .en(w2), .clk(clk), .Q(q2));  // open: clr
  Register #(.width(32)) register_18 (.D(rd_data_in), .en(w6), .clk(clk), .Q(q6));  // open: clr
  Register #(.width(32)) register_19 (.D(rd_data_in), .en(w10), .clk(clk), .Q(q10));  // open: clr
  Register #(.width(32)) register_20 (.D(rd_data_in), .en(w14), .clk(clk), .Q(q14));  // open: clr
  Register #(.width(32)) register_21 (.D(rd_data_in), .en(w18), .clk(clk), .Q(q18));  // open: clr
  Register #(.width(32)) register_22 (.D(rd_data_in), .en(w22), .clk(clk), .Q(q22));  // open: clr
  Register #(.width(32)) register_23 (.D(rd_data_in), .en(w26), .clk(clk), .Q(q26));  // open: clr
  Register #(.width(32)) register_24 (.D(rd_data_in), .en(w30), .clk(clk), .Q(q30));  // open: clr
  Register #(.width(32)) register_25 (.D(rd_data_in), .en(w3), .clk(clk), .Q(q3));  // open: clr
  Register #(.width(32)) register_26 (.D(rd_data_in), .en(w7), .clk(clk), .Q(q7));  // open: clr
  Register #(.width(32)) register_27 (.D(rd_data_in), .en(w11), .clk(clk), .Q(q11));  // open: clr
  Register #(.width(32)) register_28 (.D(rd_data_in), .en(w15), .clk(clk), .Q(q15));  // open: clr
  Register #(.width(32)) register_29 (.D(rd_data_in), .en(w19), .clk(clk), .Q(q19));  // open: clr
  Register #(.width(32)) register_30 (.D(rd_data_in), .en(w23), .clk(clk), .Q(q23));  // open: clr
  Register #(.width(32)) register_31 (.D(rd_data_in), .en(w27), .clk(clk), .Q(q27));  // open: clr
  Register #(.width(32)) register_32 (.D(rd_data_in), .en(w31), .clk(clk), .Q(q31));  // open: clr
endmodule

module ByteAddrMemory (
  input  mem_write_en,
  input  [24:0] addr,
  input  [31:0] write_data,
  input  [1:0] access_size,
  output [31:0] read_data
);

  wire clk, memorylogic_1_byte_0, memorylogic_1_byte_1, memorylogic_1_byte_2, memorylogic_1_byte_3;
  wire [7:0] multiplexer_1_out, ram_1_dout_2, ram_1_dout_3;
  wire [15:0] multiplexer_2_out, ram_1_dout;
  wire [31:0] bit_extender_1_out, bit_extender_2_out;

  Clock u_clk (.out(clk));
  MemoryLogic memorylogic_1 (
    .A(access_size[1]), .B(access_size[0]), .C(addr[1]), .D(addr[0]), .byte_0(memorylogic_1_byte_0),
    .byte_1(memorylogic_1_byte_1), .byte_2(memorylogic_1_byte_2), .byte_3(memorylogic_1_byte_3));
  RAM #(.addrWidth(23), .asyncread("true"), .byteenables("byteEnables"), .dataWidth(32), .\type ("nonvolatile")) ram_1 (
    .addr(addr[24:2]), .we(mem_write_en), .oe(1'b1), .clk(clk), .din(write_data),
    .dout({ram_1_dout, ram_1_dout_3, ram_1_dout_2}), .be3(memorylogic_1_byte_3), .be2(memorylogic_1_byte_2),
    .be1(memorylogic_1_byte_1), .be0(memorylogic_1_byte_0));
  Multiplexer #(.select(2), .width(8)) multiplexer_1 (
    .in0(ram_1_dout_2), .in1(ram_1_dout_3), .in2(ram_1_dout[7:0]), .in3(ram_1_dout[15:8]),
    .out(multiplexer_1_out), .sel(addr[1:0]));
  Multiplexer #(.width(16)) multiplexer_2 (
    .in0(ram_1_dout), .in1({ram_1_dout_3, ram_1_dout_2}), .out(multiplexer_2_out), .sel(addr[1]));
  assign bit_extender_1_out = {{24{multiplexer_1_out[7]}}, multiplexer_1_out};  // Bit_Extender bit_extender_1
  assign bit_extender_2_out = {{16{multiplexer_2_out[15]}}, multiplexer_2_out};  // Bit_Extender bit_extender_2
  Multiplexer #(.select(2), .width(32)) multiplexer_3 (
    .in0(bit_extender_1_out), .in1(bit_extender_2_out), .in2({ram_1_dout, ram_1_dout_3, ram_1_dout_2}),
    .out(read_data), .sel(access_size));  // open: in3

  // Other names for the same wires on the sheet: B = access_size[0]; A = access_size[1]; ADDR_t[1:0] = addr[1:0];
  //   D = addr[0]; C = addr[1]
endmodule

module MemoryLogic (
  input  A,
  input  B,
  input  C,
  input  D,
  output byte_0,
  output byte_1,
  output byte_2,
  output byte_3
);

  wire and_4_out, and_5_out, and_6_out, and_7_out, and_8_out, and_9_out, and_10_out, and_11_out, byte_access,
       half_access, not_1_out, not_2_out, not_3_out, not_4_out, word_access;

  not not_1 (not_1_out, C);
  not not_2 (not_2_out, B);
  not not_3 (not_3_out, A);
  not not_4 (not_4_out, D);
  and and_1 (word_access, A, not_2_out);
  and and_2 (half_access, B, not_3_out);
  and and_3 (byte_access, not_3_out, not_2_out);
  and and_4 (and_4_out, half_access, not_1_out);
  and and_5 (and_5_out, byte_access, not_1_out, not_4_out);
  and and_6 (and_6_out, half_access, not_1_out);
  and and_7 (and_7_out, byte_access, not_1_out, D);
  and and_8 (and_8_out, half_access, C);
  and and_9 (and_9_out, byte_access, C, not_4_out);
  and and_10 (and_10_out, half_access, C);
  and and_11 (and_11_out, byte_access, C, D);
  or or_1 (byte_0, word_access, and_4_out, and_5_out);
  or or_2 (byte_1, word_access, and_6_out, and_7_out);
  or or_3 (byte_2, word_access, and_8_out, and_9_out);
  or or_4 (byte_3, word_access, and_10_out, and_11_out);
endmodule

module ALU (
  input  [3:0] opcode,
  input  [31:0] A,
  input  [31:0] B,
  output zero_flag,
  output [31:0] ALU_out
);

  wire comparator_1_lt;
  wire [31:0] adder_1_out, and_1_out, bit_extender_1_out, or_1_out, subtractor_1_out, xor_1_out;

  Adder #(.width(32)) adder_1 (.a(A), .b(B), .out(adder_1_out));  // open: cin, cout
  Subtractor #(.width(32)) subtractor_1 (.a(A), .b(B), .out(subtractor_1_out));  // open: bin, bout
  assign and_1_out = A & B;  // AND_Gate and_1, 32 bits wide
  assign or_1_out = A | B;  // OR_Gate or_1, 32 bits wide
  Comparator #(.width(32)) comparator_1 (.a(A), .b(B), .lt(comparator_1_lt));  // open: gt, eq
  assign xor_1_out = A ^ B;  // XOR_Gate xor_1, 32 bits wide
  assign bit_extender_1_out = {{31{1'b0}}, comparator_1_lt};  // Bit_Extender bit_extender_1
  Multiplexer #(.select(4), .width(32)) multiplexer_1 (
    .in0(adder_1_out), .in1(subtractor_1_out), .in2(and_1_out), .in3(or_1_out), .in4(xor_1_out),
    .in5(bit_extender_1_out), .out(ALU_out), .sel(opcode));  // open: in6, in7, in8, in9, in10, in11, in12, in13, in14, in15
  Comparator #(.width(32)) comparator_2 (.a({32{1'b0}}), .b(ALU_out), .eq(zero_flag));  // open: gt, lt
endmodule
